# Fritzing sketch schema (saved by Fritzing 0.9.4)
circuit board: 9.44192cm x 8.26223cm

parts:
  JP3 = Header 4 [package=jst-4-pth]
  WeMos_D1_Mini2 = WeMos D1 Mini
  J5 = male pin header, 8 pins [form="♂ (male)"]
  J6 = male pin header, 8 pins [form="♂ (male)"]
  S2 = Momentary Switch [package=ksa_sealed_tac_switch]
  J7 = male pin header, 3 pins [form="♂ (male)"]
  J8 = male pin header, 3 pins [form="♂ (male)"]
  Micro_USB = male pin header, 4 pins [form="♂ (male)"]

nets:
  N1: JP3.1, JP3.2, WeMos_D1_Mini2.5V, Micro_USB.pin4
  N2: JP3.3, JP3.4, WeMos_D1_Mini2.G, J6.pin8, Micro_USB.pin1
  N3: WeMos_D1_Mini2.3V3, S2.2
  N4: WeMos_D1_Mini2.A0, S2.3
  N5: WeMos_D1_Mini2.D0, J6.pin7
  N6: WeMos_D1_Mini2.D1, J5.pin5
  N7: WeMos_D1_Mini2.D2, J6.pin5
  N8: WeMos_D1_Mini2.D4, J5.pin8
  N9: WeMos_D1_Mini2.D5, J5.pin7
  N10: WeMos_D1_Mini2.D6, J6.pin6
  N11: WeMos_D1_Mini2.D7, J5.pin1
  N12: WeMos_D1_Mini2.D8, J5.pin6
  N13: J5.pin2, J8.pin3
  N14: J5.pin3, J7.pin1
  N15: J5.pin4, J7.pin2
  N16: J6.pin1, J7.pin3
  N17: J6.pin3, J8.pin1
